// Logisim project 16_Bits_Project.circ as structural Verilog: 4 circuits, main circuit main
module main (
);

  wire and_1_out, Branch, clock_1_out, J, MR, MTR, MW, RD, RW, Zero;
  wire [1:0] ALU_SRC;
  wire [2:0] multiplexer_3_out;
  wire [3:0] ALUOP, OpCode;
  wire [11:0] rom_1_data;
  wire [15:0] adder_1_out, adder_2_out, alu_16_1_out_4, bit_extender_1_out, bit_extender_2_out,
       bit_extender_3_out, multiplexer_1_out, multiplexer_2_out, multiplexer_4_out, multiplexer_5_out,
       ram_1_dout, register_1_q, register_file_8_bits_1_reg_data_1, register_file_8_bits_1_reg_data_2;

  Multiplexer #(.width(16)) multiplexer_1 (
    .in0(multiplexer_2_out), .in1(adder_1_out), .out(multiplexer_1_out), .sel(and_1_out));
  Clock clock_1 (.out(clock_1_out));
  Register #(.width(16)) register_1 (
    .D(multiplexer_1_out), .en(1'b1), .clk(clock_1_out), .Q(register_1_q));  // open: clr
  and and_1 (and_1_out, Branch, Zero);
  Adder #(.width(16)) adder_1 (.a(register_1_q), .b(bit_extender_3_out), .out(adder_1_out));  // open: cin, cout
  Adder #(.width(16)) adder_2 (.a(16'h1), .b(register_1_q), .out(adder_2_out));  // open: cin, cout
  Multiplexer #(.width(16)) multiplexer_2 (
    .in0(adder_2_out), .in1(bit_extender_2_out), .out(multiplexer_2_out), .sel(J));
  ROM #(.addrWidth(16), .dataWidth(16)) rom_1 (.addr(register_1_q), .data({OpCode, rom_1_data}));
  Multiplexer #(.width(3)) multiplexer_3 (
    .in0(rom_1_data[5:3]), .in1(rom_1_data[8:6]), .out(multiplexer_3_out), .sel(RD));
  assign bit_extender_1_out = {{13{1'b0}}, rom_1_data[2:0]};  // Bit_Extender bit_extender_1
  assign bit_extender_2_out = {{4{1'b0}}, rom_1_data};  // Bit_Extender bit_extender_2
  assign bit_extender_3_out = {{10{1'b0}}, rom_1_data[5:0]};  // Bit_Extender bit_extender_3
  Register_File_8_Bits register_file_8_bits_1 (
    .Read_Add_1(rom_1_data[11:9]), .Read_Add_2(rom_1_data[8:6]), .Write_add(multiplexer_3_out),
    .Write_en(RW), .Data(multiplexer_5_out), .CLK(clock_1_out),
    .Reg_Data_1(register_file_8_bits_1_reg_data_1), .Reg_Data_2(register_file_8_bits_1_reg_data_2));
  Multiplexer #(.select(2), .width(16)) multiplexer_4 (
    .in0(register_file_8_bits_1_reg_data_2), .in1(bit_extender_3_out), .in2(bit_extender_1_out),
    .out(multiplexer_4_out), .sel(ALU_SRC));  // open: in3
  Multiplexer #(.width(16)) multiplexer_5 (.in0(alu_16_1_out_4), .in1(ram_1_dout), .out(multiplexer_5_out), .sel(MTR));
  Control_Unit control_unit_1 (
    .OpCode(OpCode), .ALUOP(ALUOP), .RegWrite(RW), .RegDest(RD), .ALU_SRC(ALU_SRC), .MemRead(MR),
    .MemWrite(MW), .MemToReg(MTR), .Jump(J), .Branch(Branch));
  ALU_16 alu_16_1 (
    .A(register_file_8_bits_1_reg_data_1), .B(multiplexer_4_out), .in_3(ALUOP), .out_4(alu_16_1_out_4),
    .Zero(Zero));
  RAM #(.addrWidth(16), .dataWidth(16)) ram_1 (
    .addr(alu_16_1_out_4), .we(MW), .oe(MR), .clk(clock_1_out), .din(register_file_8_bits_1_reg_data_2),
    .dout(ram_1_dout));

  // Notes on the sheet:
  //   contents of rom_1 (hex, n*v repeats v):
  //   1040 108a 10c0 1102 84c6 308 a700 1902 46c0 b004 b00a
  //   RS
  //   RT
  //   RD
  //   Shamt
  //   Datapath for a 16 Bits Processor
endmodule

module ALU_16 (
  input  [15:0] A,
  input  [15:0] B,
  input  [3:0] in_3,
  output [15:0] out_4,
  output Zero
);

  wire comparator_1_lt;
  wire [3:0] bit_extender_1_out;
  wire [15:0] adder_1_out, adder_2_out, bit_extender_2_out, multiplexer_1_out, not_1_out, shifter_1_out,
       shifter_2_out, xor_1_out;

  assign not_1_out = ~B;  // NOT_Gate not_1, 16 bits wide
  Multiplexer #(.width(16)) multiplexer_1 (.in0(B), .in1(not_1_out), .out(multiplexer_1_out), .sel(in_3[0]));
  Bit_Extender #(.in_width(16), .out_width(4)) bit_extender_1 (.in(B), .out(bit_extender_1_out));
  Comparator #(.mode("unsigned"), .width(16)) comparator_1 (.a(A), .b(B), .lt(comparator_1_lt));  // open: gt, eq
  Adder #(.width(16)) adder_1 (.a(A), .b(multiplexer_1_out), .out(adder_1_out), .cin(in_3[0]));  // open: cout
  Adder #(.width(16)) adder_2 (.a(A), .b(16'h1), .out(adder_2_out));  // open: cin, cout
  Shifter #(.width(16)) shifter_1 (.in(A), .\dist (bit_extender_1_out), .out(shifter_1_out));
  Shifter #(.shift("lr"), .width(16)) shifter_2 (.in(A), .\dist (bit_extender_1_out), .out(shifter_2_out));
  assign xor_1_out = A ^ B;  // XOR_Gate xor_1, 16 bits wide
  assign bit_extender_2_out = {{15{comparator_1_lt}}, comparator_1_lt};  // Bit_Extender bit_extender_2
  Multiplexer #(.select(3), .width(16)) multiplexer_2 (
    .in0(adder_1_out), .in1(adder_2_out), .in2(shifter_1_out), .in3(shifter_2_out), .in4(xor_1_out),
    .in5(bit_extender_2_out), .out(out_4), .sel(in_3[3:1]));  // open: in6, in7
  nor nor_1 (Zero, out_4[0], out_4[1], out_4[2], out_4[3], out_4[4], out_4[5], out_4[6], out_4[7], out_4[8], out_4[9], out_4[10], out_4[11], out_4[12], out_4[13], out_4[14], out_4[15]);

  // Notes on the sheet:
  //   ALUOP
  //   Arithmetic Logic Unit
endmodule

module Register_File_8_Bits (
  input  [2:0] Read_Add_1,
  input  Write_en,
  input  [2:0] Write_add,
  input  [2:0] Read_Add_2,
  input  [15:0] Data,
  input  CLK,
  output [15:0] Reg_Data_1,
  output [15:0] Reg_Data_2
);

  wire decoder_1_out1, decoder_1_out2, decoder_1_out3, decoder_1_out4, decoder_1_out5, decoder_1_out6,
       decoder_1_out7;
  wire [15:0] register_1_q, register_2_q, register_3_q, register_4_q, register_5_q, register_6_q,
       register_7_q, register_8_q;

  Decoder #(.select(3)) decoder_1 (
    .out1(decoder_1_out1), .out2(decoder_1_out2), .out3(decoder_1_out3), .out4(decoder_1_out4),
    .out5(decoder_1_out5), .out6(decoder_1_out6), .out7(decoder_1_out7), .sel(Write_add), .en(Write_en));  // open: out0
  Register #(.width(16)) register_1 (.D(Data), .en(1'b0), .clk(CLK), .Q(register_1_q));  // open: clr
  Register #(.width(16)) register_2 (.D(Data), .en(decoder_1_out1), .clk(CLK), .Q(register_2_q));  // open: clr
  Register #(.width(16)) register_3 (.D(Data), .en(decoder_1_out2), .clk(CLK), .Q(register_3_q));  // open: clr
  Register #(.width(16)) register_4 (.D(Data), .en(decoder_1_out3), .clk(CLK), .Q(register_4_q));  // open: clr
  Register #(.width(16)) register_5 (.D(Data), .en(decoder_1_out4), .clk(CLK), .Q(register_5_q));  // open: clr
  Register #(.width(16)) register_6 (.D(Data), .en(decoder_1_out5), .clk(CLK), .Q(register_6_q));  // open: clr
  Register #(.width(16)) register_7 (.D(Data), .en(decoder_1_out6), .clk(CLK), .Q(register_7_q));  // open: clr
  Register #(.width(16)) register_8 (.D(Data), .en(decoder_1_out7), .clk(CLK), .Q(register_8_q));  // open: clr
  Multiplexer #(.select(3), .width(16)) multiplexer_1 (
    .in0(register_1_q), .in1(register_2_q), .in2(register_3_q), .in3(register_4_q), .in4(register_5_q),
    .in5(register_6_q), .in6(register_7_q), .in7(register_8_q), .out(Reg_Data_1), .sel(Read_Add_1));
  Multiplexer #(.select(3), .width(16)) multiplexer_2 (
    .in0(register_1_q), .in1(register_2_q), .in2(register_3_q), .in3(register_4_q), .in4(register_5_q),
    .in5(register_6_q), .in6(register_7_q), .in7(register_8_q), .out(Reg_Data_2), .sel(Read_Add_2));

  // Notes on the sheet:
  //   Register File
endmodule

module Control_Unit (
  input  [3:0] OpCode,
  output [3:0] ALUOP,
  output RegWrite,
  output RegDest,
  output [1:0] ALU_SRC,
  output MemRead,
  output MemWrite,
  output MemToReg,
  output Jump,
  output Branch
);

  wire and_1_out, and_2_out, and_3_out, and_4_out, and_5_out, and_6_out, and_7_out, and_8_out, and_9_out,
       and_10_out, and_11_out, and_12_out, and_13_out, and_14_out, and_15_out, and_16_out, and_17_out,
       and_18_out, and_19_out, and_22_out, and_23_out, not_1_out, not_2_out, not_3_out, not_4_out;

  not not_1 (not_1_out, OpCode[3]);
  not not_2 (not_2_out, OpCode[2]);
  not not_3 (not_3_out, OpCode[1]);
  not not_4 (not_4_out, OpCode[0]);
  and and_1 (and_1_out, OpCode[2], OpCode[1], OpCode[0]);
  and and_2 (and_2_out, OpCode[3], OpCode[2]);
  and and_3 (and_3_out, not_1_out, OpCode[2], not_3_out, OpCode[0]);
  and and_4 (and_4_out, not_1_out, OpCode[2], OpCode[1], not_4_out);
  and and_5 (and_5_out, not_1_out, OpCode[2], not_4_out);
  and and_6 (and_6_out, OpCode[2], not_3_out, not_4_out);
  and and_7 (and_7_out, not_1_out, not_2_out, OpCode[1]);
  and and_8 (and_8_out, OpCode[3], not_2_out, not_3_out, not_4_out);
  and and_9 (and_9_out, OpCode[3], OpCode[2], OpCode[1], not_4_out);
  and and_10 (and_10_out, not_3_out, OpCode[0]);
  and and_11 (and_11_out, OpCode[2], not_3_out);
  and and_12 (and_12_out, not_2_out, OpCode[0]);
  and and_13 (and_13_out, not_1_out, OpCode[2], not_3_out, not_4_out);
  and and_14 (and_14_out, not_1_out, OpCode[2], not_3_out, OpCode[0]);
  and and_15 (and_15_out, OpCode[2], OpCode[1], not_4_out);
  and and_16 (and_16_out, OpCode[3], OpCode[1], OpCode[0]);
  and and_17 (and_17_out, not_2_out, OpCode[0]);
  and and_18 (and_18_out, not_1_out, OpCode[2], not_3_out, not_4_out);
  and and_19 (and_19_out, OpCode[3], OpCode[1]);
  and and_20 (MemRead, OpCode[3], not_2_out, not_3_out, OpCode[0]);
  and and_21 (MemWrite, OpCode[3], OpCode[1], not_4_out);
  and and_22 (and_22_out, OpCode[3], not_2_out);
  and and_23 (and_23_out, OpCode[3], OpCode[1]);
  and and_24 (Jump, OpCode[3], OpCode[1], OpCode[0]);
  and and_25 (Branch, OpCode[3], not_2_out, not_3_out, not_4_out);
  or or_1 (ALUOP[3], and_1_out, and_2_out);
  or or_2 (ALUOP[2], and_3_out, and_4_out);
  or or_3 (ALUOP[1], and_5_out, and_6_out);
  or or_4 (ALUOP[0], and_7_out, and_8_out, and_9_out);
  or or_5 (RegWrite, not_1_out, and_10_out, and_11_out);
  or or_6 (RegDest, and_12_out, and_13_out);
  or or_7 (ALU_SRC[1], and_14_out, and_15_out, and_16_out);
  or or_8 (ALU_SRC[0], and_17_out, and_18_out, and_19_out);
  or or_9 (MemToReg, and_22_out, and_23_out);
endmodule
