// Logisim project Pattern - Based Lock System.circ as structural Verilog: 15 circuits, main circuit main
module main (
  output out_1,
  output out_2,
  output out_3,
  output out_4,
  output out_5,
  output out_6,
  output out_7,
  output out_8,
  output out_9,
  output out_10,
  output out_11
);

  wire _0, _1, _2, _3, _4, _5, _5_input_block, _6, _7, _8, _9, a0, a1, a2, a3, a4, a5, Admin_, and_1_out,
       and_2_out, and_4_out, and_5_out, and_6_out, and_7_out, and_8_out, and_12_out, and_13_out, and_14_out,
       and_15_out, and_21_out, and_22_out, and_23_out, b0, b1, b2, b3, b4, bClock, btn, buttons, c0, c1, c2,
       c3, c4, Clear, Clear1, clock_1_out, CLR, CLRX, Comparator_1_a_b, Comparator_2_a_b, Comparator_3_a_b,
       CP, d0, d1, d2, d3, d4, d_ff_1_q, d_ff_2_q, demultiplexer_4_out0, demultiplexer_4_out1,
       demultiplexer_4_out2, demultiplexer_4_out3, demultiplexer_4_out4, e0, e1, e2, e3, e4, e5, EnableComp,
       EP, f0, f1, f2, f3, f4, g0, g1, g2, g3, g4, g5, multiplexer_7_out, multiplexer_18_out,
       multiplexer_19_out, multiplexer_20_out, multiplexer_21_out, multiplexer_22_out, n5_input_counter_1_y,
       not_1_out, not_2_out, not_3_out, not_4_out, not_5_out, not_6_out, not_7_out, not_8_out, not_9_out,
       not_10_out, not_13_out, not_14_out, not_15_out, not_16_out, not_17_out, not_18_out, not_19_out,
       not_20_out, not_21_out, not_22_out, not_23_out, not_24_out, not_25_out, NP, nxt, or_1_out, or_2_out,
       or_8_out, or_9_out, or_10_out, or_11_out, or_12_out, p0, pass1, pass2, pass3, pass_1, pass_2, pass_3,
       Save, Save_, timer_1_out_3, xor_1_out, xor_2_out, xor_3_out, xor_4_out, xor_5_out, xor_6_out,
       xor_7_out, xor_8_out, xor_9_out, xor_10_out;
  wire [1:0] Pass_2_or_3_out_4;
  wire [2:0] Next;
  wire [2:2] Delay_out_2;
  wire [3:0] demultiplexer_1_out0, demultiplexer_1_out1, demultiplexer_2_out0, demultiplexer_2_out1,
       demultiplexer_2_out2, demultiplexer_2_out3, demultiplexer_2_out4, dis1, dis2, dis3, dis4, dis5,
       Keypad_to_EX3_b0, mr_memory_1_regaout, mr_memory_1_regbout, mr_memory_1_regcout, mr_memory_1_regdout,
       mr_memory_1_regeout, multiplexer_1_out, multiplexer_8_out, multiplexer_9_out, multiplexer_10_out,
       multiplexer_11_out, multiplexer_12_out, multiplexer_13_out, multiplexer_14_out, multiplexer_15_out,
       multiplexer_16_out, multiplexer_17_out, pa1, pa2, pa3, pa4, pa5, shift_register_1__0_2,
       shift_register_2__0_2, shift_register_3__0_2, shift_register_4__0_2, shift_register_5__0_2, undriven,
       undriven_2, undriven_3, undriven_4, undriven_5, undriven_6, undriven_7, undriven_8, z1, z2, z3, z4,
       z5, z6, z7, z8, z9, z10, z11, z12, z13, z14, z15;

  or or_1 (or_1_out, buttons, Clear1);
  not not_1 (not_1_out, out_1);
  not not_2 (not_2_out, and_1_out);
  and and_1 (and_1_out, or_1_out, not_1_out);
  and and_2 (and_2_out, not_2_out, clock_1_out);
  and and_3 (bClock, or_2_out, buttons);
  Button u__1 (.out(_1));
  Button u__4 (.out(_4));
  Button u__7 (.out(_7));
  Button u_Save (.out(Save_));
  Button Admin (.out(Admin_));
  Button p1 (.out(pass_1));
  Button p2 (.out(pass_2));
  Button p3 (.out(pass_3));
  D_Flip_Flop d_ff_1 (.clk(and_1_out), .D(and_1_out), .Q(d_ff_1_q), .reset(and_2_out));  // open: Qn, preset, en
  or or_2 (or_2_out, and_4_out, d_ff_2_q);
  Button u__2 (.out(_2));
  Button u__5 (.out(_5));
  Button u__8 (.out(_8));
  Button u__0 (.out(_0));
  Clock clock_1 (.out(clock_1_out));
  and and_4 (and_4_out, out_2, not_3_out);
  not not_3 (not_3_out, out_9);
  D_Flip_Flop d_ff_2 (.clk(buttons), .D(not_4_out), .Q(d_ff_2_q));  // open: Qn, preset, en, reset
  not not_4 (not_4_out, out_3);
  Button u__3 (.out(_3));
  Button u__6 (.out(_6));
  Button u__9 (.out(_9));
  Button u_CLR (.out(Clear1));
  Button Edit (.out(EP));
  Button Change_Password (.out(CP));
  Timer timer_1 (.CLK(clock_1_out), .X(d_ff_1_q), .out_3(timer_1_out_3));
  Button Next_Bit (.out(NP));
  and and_5 (and_5_out, timer_1_out_3, not_5_out);
  not not_5 (not_5_out, out_1);
  or or_3 (buttons, _1, _2, _0, _3, _4, _5, _6, _7, _8, _9);
  not not_6 (not_6_out, out_1);
  not not_7 (not_7_out, and_5_out);
  not not_8 (not_8_out, buttons);
  Keypad Keypad_to_EX3 (
    .in_1(_0), .in_2(_1), .in_3(_2), .in_4(_3), .in_5(_4), .in_6(_5), .in_7(_6), .in_8(_7), .in_9(_8),
    .in_10(_9), .b0(Keypad_to_EX3_b0[0]), .b1(Keypad_to_EX3_b0[1]), .b2(Keypad_to_EX3_b0[2]),
    .b3(Keypad_to_EX3_b0[3]));
  or or_4 (Clear, Clear1, and_6_out);
  and and_6 (and_6_out, not_7_out, not_6_out);
  _5_Input_Counter u_5_input_counter_1 (.Clk(not_8_out), .Clear(CLR), .X(_5_input_block), .Y(n5_input_counter_1_y));
  _7_Segment_Display u_7_segment_display_1 (.g(g4), .f(f4), .a(a4), .b(b4), .e(e4), .d(d4), .c(c4));  // open: dp
  and and_7 (and_7_out, n5_input_counter_1_y, buttons);
  not not_9 (not_9_out, out_10);
  not not_10 (not_10_out, out_11);
  not not_11 (btn, and_7_out);
  _7_Segment_Display u_7_segment_display_2 (.g(g3), .f(f3), .a(a3), .b(b3), .e(e3), .d(d3), .c(c3));  // open: dp
  and and_8 (and_8_out, not_9_out, not_10_out);
  and and_9 (out_8, and_8_out, out_1);
  or or_5 (EnableComp, shift_register_1__0_2[3], shift_register_1__0_2[2], shift_register_1__0_2[1], shift_register_1__0_2[0]);
  Multiplexer #(.width(4), .enable("false")) multiplexer_1 (
    .in0(Keypad_to_EX3_b0), .in1(4'b0000), .out(multiplexer_1_out), .sel(btn));
  _7_Segment_Display u_7_segment_display_3 (.g(g2), .f(f2), .a(a2), .b(b2), .e(e2), .d(d2), .c(c2));  // open: dp
  Demultiplexer #(.width(4), .enable("false")) demultiplexer_1 (
    .out0(demultiplexer_1_out0), .out1(demultiplexer_1_out1), .in(multiplexer_1_out), .sel(out_1));
  _7_Segment_Display u_7_segment_display_4 (
    .g(g5), .f(1'b1), .a(a5), .b(1'b1), .e(e5), .d(1'b1), .c(1'b1));  // open: dp
  T_Flip_Flop t_ff_1 (.clk(Admin_), .T(Admin_), .Q(out_1));  // open: Qn, preset, reset, en
  and and_10 (out_10, Pass_2_or_3_out_4[0], out_1);
  and and_11 (out_11, Pass_2_or_3_out_4[1], out_1);
  _7_Segment_Display u_7_segment_display_5 (.g(g1), .f(f1), .a(a1), .b(b1), .e(e1), .d(d1), .c(c1));  // open: dp
  not not_12 (_5_input_block, out_1);
  or or_6 (p0, Admin_, pass1);
  Shift_Register shift_register_1 (
    ._0(demultiplexer_1_out0[0]), ._1(demultiplexer_1_out0[1]), ._2(demultiplexer_1_out0[2]),
    ._3(demultiplexer_1_out0[3]), .Clk(btn), .Clear(CLR), ._0_2(shift_register_1__0_2[0]),
    ._1_2(shift_register_1__0_2[1]), ._2_2(shift_register_1__0_2[2]), ._3_2(shift_register_1__0_2[3]));
  Shift_Register shift_register_2 (
    ._0(shift_register_1__0_2[0]), ._1(shift_register_1__0_2[1]), ._2(shift_register_1__0_2[2]),
    ._3(shift_register_1__0_2[3]), .Clk(btn), .Clear(CLR), ._0_2(shift_register_2__0_2[0]),
    ._1_2(shift_register_2__0_2[1]), ._2_2(shift_register_2__0_2[2]), ._3_2(shift_register_2__0_2[3]));
  Shift_Register shift_register_3 (
    ._0(shift_register_2__0_2[0]), ._1(shift_register_2__0_2[1]), ._2(shift_register_2__0_2[2]),
    ._3(shift_register_2__0_2[3]), .Clk(btn), .Clear(CLR), ._0_2(shift_register_3__0_2[0]),
    ._1_2(shift_register_3__0_2[1]), ._2_2(shift_register_3__0_2[2]), ._3_2(shift_register_3__0_2[3]));
  Shift_Register shift_register_4 (
    ._0(shift_register_3__0_2[0]), ._1(shift_register_3__0_2[1]), ._2(shift_register_3__0_2[2]),
    ._3(shift_register_3__0_2[3]), .Clk(btn), .Clear(CLR), ._0_2(shift_register_4__0_2[0]),
    ._1_2(shift_register_4__0_2[1]), ._2_2(shift_register_4__0_2[2]), ._3_2(shift_register_4__0_2[3]));
  Shift_Register shift_register_5 (
    ._0(shift_register_4__0_2[0]), ._1(shift_register_4__0_2[1]), ._2(shift_register_4__0_2[2]),
    ._3(shift_register_4__0_2[3]), .Clk(btn), .Clear(CLR), ._0_2(shift_register_5__0_2[0]),
    ._1_2(shift_register_5__0_2[1]), ._2_2(shift_register_5__0_2[2]), ._3_2(shift_register_5__0_2[3]));
  password_select Pass_2_or_3 (
    .in_1(pass1), .in_2(pass2), .in_3(pass3), .out_4(Pass_2_or_3_out_4[0]), .out_5(Pass_2_or_3_out_4[1]));
  Multiplexer #(.width(4), .enable("false")) multiplexer_2 (
    .in0(shift_register_1__0_2), .in1(pa1), .out(dis1), .sel(out_1));
  Multiplexer #(.width(4), .enable("false")) multiplexer_3 (
    .in0(shift_register_2__0_2), .in1(pa2), .out(dis2), .sel(out_1));
  Multiplexer #(.width(4), .enable("false")) multiplexer_4 (
    .in0(shift_register_3__0_2), .in1(pa3), .out(dis3), .sel(out_1));
  Multiplexer #(.width(4), .enable("false")) multiplexer_5 (
    .in0(shift_register_4__0_2), .in1(pa4), .out(dis4), .sel(out_1));
  Multiplexer #(.width(4), .enable("false")) multiplexer_6 (
    .in0(shift_register_5__0_2), .in1(pa5), .out(dis5), .sel(out_1));
  _7_Segment_Display u_7_segment_display_6 (.g(g0), .f(f0), .a(a0), .b(b0), .e(e0), .d(d0), .c(c0));  // open: dp
  and and_12 (and_12_out, out_1, CP);
  and and_13 (and_13_out, bClock, out_9);
  and and_14 (and_14_out, EP, out_9);
  and and_15 (and_15_out, out_9, Admin_);
  or or_7 (CLR, Clear, and_12_out);
  T_Flip_Flop t_ff_2 (.clk(EP), .T(EP), .Q(out_2), .reset(not_13_out));  // open: Qn, preset, en
  not not_13 (not_13_out, out_1);
  EX3_to_seven_segment ex3_to_seven_segment_1 (
    .z(dis1[0]), .y(dis1[1]), .x(dis1[2]), .w(dis1[3]), .a(a0), .b(b0), .c(c0), .d(d0), .e(e0), .f(f0), .g(g0));
  EX3_to_seven_segment ex3_to_seven_segment_2 (
    .z(dis2[0]), .y(dis2[1]), .x(dis2[2]), .w(dis2[3]), .a(a1), .b(b1), .c(c1), .d(d1), .e(e1), .f(f1), .g(g1));
  EX3_to_seven_segment ex3_to_seven_segment_3 (
    .z(dis3[0]), .y(dis3[1]), .x(dis3[2]), .w(dis3[3]), .a(a2), .b(b2), .c(c2), .d(d2), .e(e2), .f(f2), .g(g2));
  EX3_to_seven_segment ex3_to_seven_segment_4 (
    .z(dis4[0]), .y(dis4[1]), .x(dis4[2]), .w(dis4[3]), .a(a3), .b(b3), .c(c3), .d(d3), .e(e3), .f(f3), .g(g3));
  EX3_to_seven_segment ex3_to_seven_segment_5 (
    .z(dis5[0]), .y(dis5[1]), .x(dis5[2]), .w(dis5[3]), .a(a4), .b(b4), .c(c4), .d(d4), .e(e4), .f(f4), .g(g4));
  T_Flip_Flop t_ff_3 (.clk(or_8_out), .T(CP), .Q(out_9), .reset(not_14_out));  // open: Qn, preset, en
  or or_8 (or_8_out, EP, CP);
  not not_14 (not_14_out, out_2);
  or or_9 (or_9_out, and_13_out, and_14_out, and_15_out);
  Multiplexer #(.enable("false")) multiplexer_7 (.in0(NP), .in1(bClock), .out(multiplexer_7_out), .sel(out_9));
  or or_10 (or_10_out, or_9_out, Save);
  Next next_1 (.Clk(not_15_out), .X(multiplexer_7_out), .C(Next[0]), .B(Next[1]), .A(Next[2]), .Clear(CLRX));
  not not_15 (not_15_out, multiplexer_7_out);
  Demultiplexer #(.select(3), .width(4)) demultiplexer_2 (
    .out0(demultiplexer_2_out0), .out1(demultiplexer_2_out1), .out2(demultiplexer_2_out2),
    .out3(demultiplexer_2_out3), .out4(demultiplexer_2_out4), .in(demultiplexer_1_out1), .sel(Next));  // open: out5, out6, out7, en
  Demultiplexer #(.select(3), .enable("false")) demultiplexer_3 (
    .out0(out_7), .out1(out_6), .out2(out_5), .out3(out_4), .out4(out_3), .in(out_2), .sel(Next));  // open: out5, out6, out7
  Mr_Memory mr_memory_1 (
    .in_2(out_9), .RegAIn(pa1), .RegBIn(pa2), .RegCIn(pa3), .RegDIn(pa4), .RegEIn(pa5), .Clk(or_10_out),
    .Mode(Pass_2_or_3_out_4), .po1(z1), .po2(z2), .po3(z3), .po4(z4), .po5(z5),
    .RegAOut(mr_memory_1_regaout), .RegBOut(mr_memory_1_regbout), .po6(z6), .po7(z7), .po8(z8),
    .RegCOut(mr_memory_1_regcout), .po9(z9), .p10(z10), .RegDOut(mr_memory_1_regdout),
    .RegEOut(mr_memory_1_regeout), .p11(z11), .p12(z12), .p13(z13), .p14(z14), .p15(z15), .Clear(CP));
  Multiplexer #(.width(4), .enable("false")) multiplexer_8 (
    .in0(demultiplexer_2_out0), .in1(Keypad_to_EX3_b0), .out(multiplexer_8_out), .sel(out_9));
  nots Delay (.in_1(bClock), .out_2(Delay_out_2[2]));
  not not_16 (not_16_out, out_2);
  not not_17 (not_17_out, out_9);
  or or_11 (or_11_out, Next[0], Next[1], Next[2]);
  and and_16 (nxt, or_11_out, not_18_out);
  not not_18 (not_18_out, out_9);
  and and_17 (pass1, not_16_out, pass_1);
  and and_18 (pass2, not_16_out, pass_2);
  and and_19 (pass3, not_16_out, pass_3);
  and and_20 (Save, Save_, not_17_out);
  Multiplexer #(.select(2), .width(4), .enable("false")) multiplexer_9 (
    .in0(mr_memory_1_regaout), .in1(multiplexer_8_out), .in3(mr_memory_1_regaout), .out(multiplexer_9_out),
    .sel({nxt, out_2}));  // open: in2
  Multiplexer #(.select(3), .width(4), .enable("false")) multiplexer_10 (
    .in0(mr_memory_1_regbout), .in1(undriven), .in2(undriven_5), .in7(demultiplexer_2_out1),
    .out(multiplexer_10_out), .sel({Delay_out_2[2], nxt, out_2}));  // open: in3, in4, in5, in6
  Multiplexer #(.select(3), .width(4), .enable("false")) multiplexer_11 (
    .in0(mr_memory_1_regcout), .in1(undriven_2), .in2(undriven_6), .in7(demultiplexer_2_out2),
    .out(multiplexer_11_out), .sel({Delay_out_2[2], nxt, out_2}));  // open: in3, in4, in5, in6
  Multiplexer #(.select(3), .width(4), .enable("false")) multiplexer_12 (
    .in0(mr_memory_1_regdout), .in1(undriven_3), .in2(undriven_7), .in7(demultiplexer_2_out3),
    .out(multiplexer_12_out), .sel({Delay_out_2[2], nxt, out_2}));  // open: in3, in4, in5, in6
  Multiplexer #(.select(3), .width(4), .enable("false")) multiplexer_13 (
    .in0(mr_memory_1_regeout), .in1(undriven_4), .in2(undriven_8), .in7(demultiplexer_2_out4),
    .out(multiplexer_13_out), .sel({Delay_out_2[2], nxt, out_2}));  // open: in3, in4, in5, in6
  not not_19 (not_19_out, out_2);
  and and_21 (and_21_out, p0, not_19_out);
  and and_22 (and_22_out, not_19_out, pass2);
  and and_23 (and_23_out, not_19_out, pass3);
  Multiplexer #(.width(4), .enable("false")) multiplexer_14 (
    .in0(multiplexer_10_out), .in1(pa1), .out(multiplexer_14_out), .sel(out_9));
  Multiplexer #(.width(4), .enable("false")) multiplexer_15 (
    .in0(multiplexer_11_out), .in1(pa2), .out(multiplexer_15_out), .sel(out_9));
  Multiplexer #(.width(4), .enable("false")) multiplexer_16 (
    .in0(multiplexer_12_out), .in1(pa3), .out(multiplexer_16_out), .sel(out_9));
  Multiplexer #(.width(4), .enable("false")) multiplexer_17 (
    .in0(multiplexer_13_out), .in1(pa4), .out(multiplexer_17_out), .sel(out_9));
  or or_12 (or_12_out, and_21_out, and_22_out, and_23_out);
  xor xor_1 (xor_1_out, or_12_out, xor_6_out);
  xor xor_2 (xor_2_out, or_12_out, xor_7_out);
  xor xor_3 (xor_3_out, or_12_out, xor_8_out);
  xor xor_4 (xor_4_out, or_12_out, xor_9_out);
  xor xor_5 (xor_5_out, or_12_out, xor_10_out);
  or or_13 (CLRX, CLR, or_12_out, not_20_out);
  not not_20 (not_20_out, out_1);
  Shift_Register shift_register_6 (
    ._0(multiplexer_9_out[0]), ._1(multiplexer_9_out[1]), ._2(multiplexer_9_out[2]),
    ._3(multiplexer_9_out[3]), .Clk(multiplexer_19_out), .Clear(CLRX), ._0_2(pa1[0]), ._1_2(pa1[1]),
    ._2_2(pa1[2]), ._3_2(pa1[3]));
  xor xor_6 (xor_6_out, or_12_out, demultiplexer_4_out0);
  Shift_Register shift_register_7 (
    ._0(multiplexer_14_out[0]), ._1(multiplexer_14_out[1]), ._2(multiplexer_14_out[2]),
    ._3(multiplexer_14_out[3]), .Clk(multiplexer_18_out), .Clear(CLRX), ._0_2(pa2[0]), ._1_2(pa2[1]),
    ._2_2(pa2[2]), ._3_2(pa2[3]));
  xor xor_7 (xor_7_out, or_12_out, demultiplexer_4_out1);
  Shift_Register shift_register_8 (
    ._0(multiplexer_15_out[0]), ._1(multiplexer_15_out[1]), ._2(multiplexer_15_out[2]),
    ._3(multiplexer_15_out[3]), .Clk(multiplexer_20_out), .Clear(CLRX), ._0_2(pa3[0]), ._1_2(pa3[1]),
    ._2_2(pa3[2]), ._3_2(pa3[3]));
  xor xor_8 (xor_8_out, or_12_out, demultiplexer_4_out2);
  Shift_Register shift_register_9 (
    ._0(multiplexer_16_out[0]), ._1(multiplexer_16_out[1]), ._2(multiplexer_16_out[2]),
    ._3(multiplexer_16_out[3]), .Clk(multiplexer_21_out), .Clear(CLRX), ._0_2(pa4[0]), ._1_2(pa4[1]),
    ._2_2(pa4[2]), ._3_2(pa4[3]));
  xor xor_9 (xor_9_out, or_12_out, demultiplexer_4_out3);
  Shift_Register shift_register_10 (
    ._0(multiplexer_17_out[0]), ._1(multiplexer_17_out[1]), ._2(multiplexer_17_out[2]),
    ._3(multiplexer_17_out[3]), .Clk(multiplexer_22_out), .Clear(CLRX), ._0_2(pa5[0]), ._1_2(pa5[1]),
    ._2_2(pa5[2]), ._3_2(pa5[3]));
  xor xor_10 (xor_10_out, or_12_out, demultiplexer_4_out4);
  Multiplexer #(.enable("false")) multiplexer_18 (
    .in0(xor_2_out), .in1(not_22_out), .out(multiplexer_18_out), .sel(out_9));
  Multiplexer #(.enable("false")) multiplexer_19 (
    .in0(xor_1_out), .in1(not_21_out), .out(multiplexer_19_out), .sel(out_9));
  not not_21 (not_21_out, bClock);
  not not_22 (not_22_out, bClock);
  Multiplexer #(.enable("false")) multiplexer_20 (
    .in0(xor_3_out), .in1(not_23_out), .out(multiplexer_20_out), .sel(out_9));
  not not_23 (not_23_out, bClock);
  Multiplexer #(.enable("false")) multiplexer_21 (
    .in0(xor_4_out), .in1(not_24_out), .out(multiplexer_21_out), .sel(out_9));
  not not_24 (not_24_out, bClock);
  Multiplexer #(.enable("false")) multiplexer_22 (
    .in0(xor_5_out), .in1(not_25_out), .out(multiplexer_22_out), .sel(out_9));
  not not_25 (not_25_out, bClock);
  Mr_Comparator Comparator_1 (
    .A0(dis1), .in_2(EnableComp), .B0(z1), .A1(dis2), .B1(z2), .A2(dis3), .B2(z3), .A3(z4), .B3(dis4),
    .A4(dis5), .B4(z5), .A_B(Comparator_1_a_b));
  Mr_Comparator Comparator_2 (
    .A0(dis1), .in_2(EnableComp), .B0(z6), .A1(dis2), .B1(z7), .A2(dis3), .B2(z8), .A3(z9), .B3(dis4),
    .A4(dis5), .B4(z10), .A_B(Comparator_2_a_b));
  Mr_Comparator Comparator_3 (
    .A0(dis1), .in_2(EnableComp), .B0(z11), .A1(dis2), .B1(z12), .A2(dis3), .B2(z13), .A3(z14), .B3(dis4),
    .A4(dis5), .B4(z15), .A_B(Comparator_3_a_b));
  Demultiplexer #(.select(3)) demultiplexer_4 (
    .out0(demultiplexer_4_out0), .out1(demultiplexer_4_out1), .out2(demultiplexer_4_out2),
    .out3(demultiplexer_4_out3), .out4(demultiplexer_4_out4), .in(btn), .sel(Next));  // open: out5, out6, out7, en
  or or_14 (g5, Comparator_1_a_b, Comparator_2_a_b, Comparator_3_a_b);
  not not_26 (a5, g5);
  not not_27 (e5, g5);

  // Other names for the same wires on the sheet: Edit = out_2; Admin = out_1; auto = out_9; l = out_3; m = out_4;
  //   n = out_5; o = out_6; p = out_7; p01 = out_8; p02 = out_10; p03 = out_11; Reset = CP

  // Notes on the sheet:
  //   Change Password Mode Will Delete The Old Password And Overwrite it. No need to save in that mode.
  //   If you edit a bit using next bit. Save it or that will not be recorded
  //   Admin Mode:
  //   b0
  //   b3
  //   Clock
  //   Output
endmodule

module EX3_to_seven_segment (
  input  z,
  input  y,
  input  x,
  input  w,
  output a,
  output b,
  output c,
  output d,
  output e,
  output f,
  output g
);

  wire and_1_out, and_2_out, and_3_out, and_4_out, and_5_out, and_6_out, and_7_out, and_8_out, and_9_out,
       and_10_out, and_11_out, and_12_out, and_13_out, and_14_out, and_15_out, and_16_out, and_17_out,
       and_18_out, and_19_out, and_20_out, not_1_out, not_2_out, not_3_out, not_4_out, not_5_out, not_6_out,
       not_7_out, not_8_out, not_9_out, not_10_out, not_11_out, not_12_out;

  not not_1 (not_1_out, x);
  and and_1 (and_1_out, not_1_out, y, z);
  and and_2 (and_2_out, x, not_2_out, z);
  not not_2 (not_2_out, y);
  and and_3 (and_3_out, x, y, not_3_out);
  not not_3 (not_3_out, z);
  and and_4 (and_4_out, y, z);
  and and_5 (and_5_out, w, y);
  and and_6 (and_6_out, y, z);
  and and_7 (and_7_out, x, not_4_out);
  not not_4 (not_4_out, z);
  not not_5 (not_5_out, x);
  and and_8 (and_8_out, not_5_out, y, z);
  not not_6 (not_6_out, y);
  and and_9 (and_9_out, x, not_6_out, z);
  and and_10 (and_10_out, x, y, not_7_out);
  not not_7 (not_7_out, z);
  and and_11 (and_11_out, w, not_8_out);
  not not_8 (not_8_out, y);
  not not_9 (not_9_out, x);
  and and_12 (and_12_out, not_9_out, y, z);
  not not_10 (not_10_out, y);
  and and_13 (and_13_out, x, not_10_out, z);
  and and_14 (and_14_out, w, z);
  and and_15 (and_15_out, y, z);
  and and_16 (and_16_out, w, not_11_out);
  not not_11 (not_11_out, y);
  and and_17 (and_17_out, x, z);
  and and_18 (and_18_out, x, y);
  and and_19 (and_19_out, w, not_12_out);
  not not_12 (not_12_out, y);
  and and_20 (and_20_out, w, z);
  or or_1 (a, and_1_out, and_2_out, and_3_out, w);
  or or_2 (b, and_4_out, x, and_5_out);
  or or_3 (c, and_6_out, and_7_out, w);
  or or_4 (d, and_8_out, and_9_out, and_10_out, and_11_out);
  or or_5 (e, and_12_out, and_13_out, and_14_out);
  or or_6 (f, and_15_out, and_16_out);
  or or_7 (g, and_17_out, and_18_out, and_19_out, and_20_out);
endmodule

module Keypad (
  input  in_1,
  input  in_2,
  input  in_3,
  input  in_4,
  input  in_5,
  input  in_6,
  input  in_7,
  input  in_8,
  input  in_9,
  input  in_10,
  output b0,
  output b1,
  output b2,
  output b3
);

  or or_1 (b0, in_1, in_3, in_5, in_7, in_9);
  or or_2 (b1, in_1, in_4, in_5, in_8, in_9);
  or or_3 (b2, in_2, in_3, in_4, in_5, in_10);
  or or_4 (b3, in_10, in_9, in_8, in_7, in_6);
endmodule

module Shift_Register (
  input  _0,
  input  _1,
  input  _2,
  input  _3,
  input  Clk,
  input  Clear,
  output _0_2,
  output _1_2,
  output _2_2,
  output _3_2
);

  D_Flip_Flop d_ff_1 (.clk(Clk), .D(_0), .Q(_0_2), .reset(Clear));  // open: Qn, preset, en
  D_Flip_Flop d_ff_2 (.clk(Clk), .D(_1), .Q(_1_2), .reset(Clear));  // open: Qn, preset, en
  D_Flip_Flop d_ff_3 (.clk(Clk), .D(_2), .Q(_2_2), .reset(Clear));  // open: Qn, preset, en
  D_Flip_Flop d_ff_4 (.clk(Clk), .D(_3), .Q(_3_2), .reset(Clear));  // open: Qn, preset, en
endmodule

// Mem
module Memory_Block (
  input  I0,
  input  _1,
  input  I2,
  input  _3,
  input  Clk,
  input  CLR,
  output [3:0] _0,
  output [3:0] _1_2,
  output [3:0] _2,
  output [3:0] _3_2
);

  Shift_Register shift_register_1 (
    ._0(I0), ._1(_1), ._2(I2), ._3(_3), .Clk(Clk), .Clear(CLR), ._0_2(_0[0]), ._1_2(_0[1]), ._2_2(_0[2]),
    ._3_2(_0[3]));
  Shift_Register shift_register_2 (
    ._0(_0[0]), ._1(_0[1]), ._2(_0[2]), ._3(_0[3]), .Clk(Clk), .Clear(CLR), ._0_2(_1_2[0]), ._1_2(_1_2[1]),
    ._2_2(_1_2[2]), ._3_2(_1_2[3]));
  Shift_Register shift_register_3 (
    ._0(_1_2[0]), ._1(_1_2[1]), ._2(_1_2[2]), ._3(_1_2[3]), .Clk(Clk), .Clear(CLR), ._0_2(_2[0]),
    ._1_2(_2[1]), ._2_2(_2[2]), ._3_2(_2[3]));
  Shift_Register shift_register_4 (
    ._0(_2[0]), ._1(_2[1]), ._2(_2[2]), ._3(_2[3]), .Clk(Clk), .Clear(CLR), ._0_2(_3_2[0]), ._1_2(_3_2[1]),
    ._2_2(_3_2[2]), ._3_2(_3_2[3]));
endmodule

module _5_Input_Counter (
  input  X,
  input  Clk,
  input  Clear,
  output Y
);

  wire A_q, A_qn, and_1_out, and_2_out, and_3_out, and_4_out, and_5_out, and_6_out, B_q, B_qn, C_q, C_qn,
       or_1_out, or_2_out, or_3_out;

  and and_1 (and_1_out, B_q, C_q);
  and and_2 (and_2_out, B_q, C_qn);
  and and_3 (and_3_out, C_q, B_qn, A_qn);
  or or_1 (or_1_out, A_q, and_1_out);
  or or_2 (or_2_out, A_q, C_qn);
  or or_3 (or_3_out, and_2_out, and_3_out);
  and and_4 (and_4_out, or_1_out, X);
  and and_5 (and_5_out, X, or_3_out);
  and and_6 (and_6_out, X, or_2_out);
  D_Flip_Flop A (.clk(Clk), .D(and_4_out), .Q(A_q), .Qn(A_qn), .reset(Clear));  // open: preset, en
  D_Flip_Flop B (.clk(Clk), .D(and_5_out), .Q(B_q), .Qn(B_qn), .reset(Clear));  // open: preset, en
  D_Flip_Flop C (.clk(Clk), .D(and_6_out), .Q(C_q), .Qn(C_qn), .reset(Clear));  // open: preset, en
  or or_4 (Y, A_qn, C_qn);
endmodule

// Mem
module Mr_Memory (
  input  [1:0] Mode,
  input  in_2,
  input  [3:0] RegAIn,
  input  [3:0] RegBIn,
  input  [3:0] RegCIn,
  input  [3:0] RegDIn,
  input  [3:0] RegEIn,
  input  Clk,
  input  Clear,
  output [3:0] po1,
  output [3:0] po2,
  output [3:0] po3,
  output [3:0] po4,
  output [3:0] po5,
  output [3:0] RegAOut,
  output [3:0] RegBOut,
  output [3:0] po6,
  output [3:0] po7,
  output [3:0] po8,
  output [3:0] RegCOut,
  output [3:0] po9,
  output [3:0] p10,
  output [3:0] RegDOut,
  output [3:0] RegEOut,
  output [3:0] p11,
  output [3:0] p12,
  output [3:0] p13,
  output [3:0] p14,
  output [3:0] p15
);

  wire demultiplexer_6_out0, demultiplexer_6_out1, demultiplexer_6_out2, demultiplexer_7_out0,
       demultiplexer_7_out1, demultiplexer_7_out2;
  wire [3:0] demultiplexer_1_out0, demultiplexer_1_out1, demultiplexer_1_out2, demultiplexer_2_out0,
       demultiplexer_2_out1, demultiplexer_2_out2, demultiplexer_3_out0, demultiplexer_3_out1,
       demultiplexer_3_out2, demultiplexer_4_out0, demultiplexer_4_out1, demultiplexer_4_out2,
       demultiplexer_5_out0, demultiplexer_5_out1, demultiplexer_5_out2;

  Demultiplexer #(.select(2), .width(4), .enable("false")) demultiplexer_1 (
    .out0(demultiplexer_1_out0), .out1(demultiplexer_1_out1), .out2(demultiplexer_1_out2), .in(RegAIn),
    .sel(Mode));  // open: out3
  Demultiplexer #(.select(2), .width(4), .enable("false")) demultiplexer_2 (
    .out0(demultiplexer_2_out0), .out1(demultiplexer_2_out1), .out2(demultiplexer_2_out2), .in(RegBIn),
    .sel(Mode));  // open: out3
  Demultiplexer #(.select(2), .width(4), .enable("false")) demultiplexer_3 (
    .out0(demultiplexer_3_out0), .out1(demultiplexer_3_out1), .out2(demultiplexer_3_out2), .in(RegCIn),
    .sel(Mode));  // open: out3
  Demultiplexer #(.select(2), .width(4), .enable("false")) demultiplexer_4 (
    .out0(demultiplexer_4_out0), .out1(demultiplexer_4_out1), .out2(demultiplexer_4_out2), .in(RegDIn),
    .sel(Mode));  // open: out3
  Demultiplexer #(.select(2), .width(4), .enable("false")) demultiplexer_5 (
    .out0(demultiplexer_5_out0), .out1(demultiplexer_5_out1), .out2(demultiplexer_5_out2), .in(RegEIn),
    .sel(Mode));  // open: out3
  Demultiplexer #(.select(2), .enable("false")) demultiplexer_6 (
    .out0(demultiplexer_6_out0), .out1(demultiplexer_6_out1), .out2(demultiplexer_6_out2), .in(Clk),
    .sel(Mode));  // open: out3
  Memory_Shift_Register memory_shift_register_1 (
    .A1(demultiplexer_1_out0[0]), .A2(demultiplexer_1_out0[1]), .A3(demultiplexer_1_out0[2]),
    .A4(demultiplexer_1_out0[3]), .B1(demultiplexer_2_out0[0]), .B2(demultiplexer_2_out0[1]),
    .B3(demultiplexer_2_out0[2]), .B4(demultiplexer_2_out0[3]), .C1(demultiplexer_3_out0[0]),
    .C2(demultiplexer_3_out0[1]), .C3(demultiplexer_3_out0[2]), .C4(demultiplexer_3_out0[3]),
    .D1(demultiplexer_4_out0[0]), .D2(demultiplexer_4_out0[1]), .D3(demultiplexer_4_out0[2]),
    .D4(demultiplexer_4_out0[3]), .E1(demultiplexer_5_out0[0]), .E2(demultiplexer_5_out0[1]),
    .E3(demultiplexer_5_out0[2]), .E4(demultiplexer_5_out0[3]), .Clk(demultiplexer_6_out0), .Mode(in_2),
    .V1(po1[0]), .V2(po1[1]), .V3(po1[2]), .V4(po1[3]), .W1(po2[0]), .W2(po2[1]), .W3(po2[2]), .W4(po2[3]),
    .X1(po3[0]), .X2(po3[1]), .X3(po3[2]), .X4(po3[3]), .Y1(po4[0]), .Y2(po4[1]), .Y3(po4[2]), .Y4(po4[3]),
    .Z1(po5[0]), .Z2(po5[1]), .Z3(po5[2]), .Z4(po5[3]), .Clear(demultiplexer_7_out0));
  Memory_Shift_Register memory_shift_register_2 (
    .A1(demultiplexer_1_out1[0]), .A2(demultiplexer_1_out1[1]), .A3(demultiplexer_1_out1[2]),
    .A4(demultiplexer_1_out1[3]), .B1(demultiplexer_2_out1[0]), .B2(demultiplexer_2_out1[1]),
    .B3(demultiplexer_2_out1[2]), .B4(demultiplexer_2_out1[3]), .C1(demultiplexer_3_out1[0]),
    .C2(demultiplexer_3_out1[1]), .C3(demultiplexer_3_out1[2]), .C4(demultiplexer_3_out1[3]),
    .D1(demultiplexer_4_out1[0]), .D2(demultiplexer_4_out1[1]), .D3(demultiplexer_4_out1[2]),
    .D4(demultiplexer_4_out1[3]), .E1(demultiplexer_5_out1[0]), .E2(demultiplexer_5_out1[1]),
    .E3(demultiplexer_5_out1[2]), .E4(demultiplexer_5_out1[3]), .Clk(demultiplexer_6_out1), .Mode(in_2),
    .V1(po6[0]), .V2(po6[1]), .V3(po6[2]), .V4(po6[3]), .W1(po7[0]), .W2(po7[1]), .W3(po7[2]), .W4(po7[3]),
    .X1(po8[0]), .X2(po8[1]), .X3(po8[2]), .X4(po8[3]), .Y1(po9[0]), .Y2(po9[1]), .Y3(po9[2]), .Y4(po9[3]),
    .Z1(p10[0]), .Z2(p10[1]), .Z3(p10[2]), .Z4(p10[3]), .Clear(demultiplexer_7_out1));
  Memory_Shift_Register memory_shift_register_3 (
    .A1(demultiplexer_1_out2[0]), .A2(demultiplexer_1_out2[1]), .A3(demultiplexer_1_out2[2]),
    .A4(demultiplexer_1_out2[3]), .B1(demultiplexer_2_out2[0]), .B2(demultiplexer_2_out2[1]),
    .B3(demultiplexer_2_out2[2]), .B4(demultiplexer_2_out2[3]), .C1(demultiplexer_3_out2[0]),
    .C2(demultiplexer_3_out2[1]), .C3(demultiplexer_3_out2[2]), .C4(demultiplexer_3_out2[3]),
    .D1(demultiplexer_4_out2[0]), .D2(demultiplexer_4_out2[1]), .D3(demultiplexer_4_out2[2]),
    .D4(demultiplexer_4_out2[3]), .E1(demultiplexer_5_out2[0]), .E2(demultiplexer_5_out2[1]),
    .E3(demultiplexer_5_out2[2]), .E4(demultiplexer_5_out2[3]), .Clk(demultiplexer_6_out2), .Mode(in_2),
    .V1(p11[0]), .V2(p11[1]), .V3(p11[2]), .V4(p11[3]), .W1(p12[0]), .W2(p12[1]), .W3(p12[2]), .W4(p12[3]),
    .X1(p13[0]), .X2(p13[1]), .X3(p13[2]), .X4(p13[3]), .Y1(p14[0]), .Y2(p14[1]), .Y3(p14[2]), .Y4(p14[3]),
    .Z1(p15[0]), .Z2(p15[1]), .Z3(p15[2]), .Z4(p15[3]), .Clear(demultiplexer_7_out2));
  Demultiplexer #(.select(2), .enable("false")) demultiplexer_7 (
    .out0(demultiplexer_7_out0), .out1(demultiplexer_7_out1), .out2(demultiplexer_7_out2), .in(Clear),
    .sel(Mode));  // open: out3
  Multiplexer #(.select(2), .width(4), .enable("false")) multiplexer_1 (
    .in0(po1), .in1(po6), .in2(p11), .out(RegAOut), .sel(Mode));  // open: in3
  Multiplexer #(.select(2), .width(4), .enable("false")) multiplexer_2 (
    .in0(po2), .in1(po7), .in2(p12), .out(RegBOut), .sel(Mode));  // open: in3
  Multiplexer #(.select(2), .width(4), .enable("false")) multiplexer_3 (
    .in0(po3), .in1(po8), .in2(p13), .out(RegCOut), .sel(Mode));  // open: in3
  Multiplexer #(.select(2), .width(4), .enable("false")) multiplexer_4 (
    .in0(po4), .in1(po9), .in2(p14), .out(RegDOut), .sel(Mode));  // open: in3
  Multiplexer #(.select(2), .width(4), .enable("false")) multiplexer_5 (
    .in0(po5), .in1(p10), .in2(p15), .out(RegEOut), .sel(Mode));  // open: in3
endmodule

module display_register (
  input  [3:0] in_1,
  output [6:0] out_2,
  output [6:0] out_3,
  output [6:0] out_4,
  output [6:0] out_5,
  output [6:0] out_6
);

  wire [3:0] shift_register_1__0_2, shift_register_2__0_2, shift_register_3__0_2, shift_register_4__0_2,
       shift_register_5__0_2;

  Shift_Register shift_register_1 (
    ._0(in_1[0]), ._1(in_1[1]), ._2(in_1[2]), ._3(in_1[3]), ._0_2(shift_register_1__0_2[0]),
    ._1_2(shift_register_1__0_2[1]), ._2_2(shift_register_1__0_2[2]), ._3_2(shift_register_1__0_2[3]));  // open: Clk, Clear
  Shift_Register shift_register_2 (
    ._0(shift_register_1__0_2[0]), ._1(shift_register_1__0_2[1]), ._2(shift_register_1__0_2[2]),
    ._3(shift_register_1__0_2[3]), ._0_2(shift_register_2__0_2[0]), ._1_2(shift_register_2__0_2[1]),
    ._2_2(shift_register_2__0_2[2]), ._3_2(shift_register_2__0_2[3]));  // open: Clk, Clear
  Shift_Register shift_register_3 (
    ._0(shift_register_2__0_2[0]), ._1(shift_register_2__0_2[1]), ._2(shift_register_2__0_2[2]),
    ._3(shift_register_2__0_2[3]), ._0_2(shift_register_3__0_2[0]), ._1_2(shift_register_3__0_2[1]),
    ._2_2(shift_register_3__0_2[2]), ._3_2(shift_register_3__0_2[3]));  // open: Clk, Clear
  Shift_Register shift_register_4 (
    ._0(shift_register_3__0_2[0]), ._1(shift_register_3__0_2[1]), ._2(shift_register_3__0_2[2]),
    ._3(shift_register_3__0_2[3]), ._0_2(shift_register_4__0_2[0]), ._1_2(shift_register_4__0_2[1]),
    ._2_2(shift_register_4__0_2[2]), ._3_2(shift_register_4__0_2[3]));  // open: Clk, Clear
  Shift_Register shift_register_5 (
    ._0(shift_register_4__0_2[0]), ._1(shift_register_4__0_2[1]), ._2(shift_register_4__0_2[2]),
    ._3(shift_register_4__0_2[3]), ._0_2(shift_register_5__0_2[0]), ._1_2(shift_register_5__0_2[1]),
    ._2_2(shift_register_5__0_2[2]), ._3_2(shift_register_5__0_2[3]));  // open: Clk, Clear
  EX3_to_seven_segment ex3_to_seven_segment_1 (
    .z(shift_register_1__0_2[0]), .y(shift_register_1__0_2[1]), .x(shift_register_1__0_2[2]),
    .w(shift_register_1__0_2[3]), .a(out_2[0]), .b(out_2[1]), .c(out_2[2]), .d(out_2[3]), .e(out_2[4]),
    .f(out_2[5]), .g(out_2[6]));
  EX3_to_seven_segment ex3_to_seven_segment_2 (
    .z(shift_register_2__0_2[0]), .y(shift_register_2__0_2[1]), .x(shift_register_2__0_2[2]),
    .w(shift_register_2__0_2[3]), .a(out_3[0]), .b(out_3[1]), .c(out_3[2]), .d(out_3[3]), .e(out_3[4]),
    .f(out_3[5]), .g(out_3[6]));
  EX3_to_seven_segment ex3_to_seven_segment_3 (
    .z(shift_register_3__0_2[0]), .y(shift_register_3__0_2[1]), .x(shift_register_3__0_2[2]),
    .w(shift_register_3__0_2[3]), .a(out_4[0]), .b(out_4[1]), .c(out_4[2]), .d(out_4[3]), .e(out_4[4]),
    .f(out_4[5]), .g(out_4[6]));
  EX3_to_seven_segment ex3_to_seven_segment_4 (
    .z(shift_register_4__0_2[0]), .y(shift_register_4__0_2[1]), .x(shift_register_4__0_2[2]),
    .w(shift_register_4__0_2[3]), .a(out_5[0]), .b(out_5[1]), .c(out_5[2]), .d(out_5[3]), .e(out_5[4]),
    .f(out_5[5]), .g(out_5[6]));
  EX3_to_seven_segment ex3_to_seven_segment_5 (
    .z(shift_register_5__0_2[0]), .y(shift_register_5__0_2[1]), .x(shift_register_5__0_2[2]),
    .w(shift_register_5__0_2[3]), .a(out_6[0]), .b(out_6[1]), .c(out_6[2]), .d(out_6[3]), .e(out_6[4]),
    .f(out_6[5]), .g(out_6[6]));
endmodule

module Memory_Shift_Register (
  input  Mode,
  input  A1,
  input  A2,
  input  A3,
  input  A4,
  input  B1,
  input  B2,
  input  B3,
  input  B4,
  input  C1,
  input  C2,
  input  C3,
  input  C4,
  input  D1,
  input  D2,
  input  D3,
  input  D4,
  input  E1,
  input  E2,
  input  E3,
  input  E4,
  input  Clk,
  input  Clear,
  output V1,
  output V2,
  output V3,
  output V4,
  output W1,
  output W2,
  output W3,
  output W4,
  output X1,
  output X2,
  output X3,
  output X4,
  output Y1,
  output Y2,
  output Y3,
  output Y4,
  output Z1,
  output Z2,
  output Z3,
  output Z4
);

  wire multiplexer_1_out, multiplexer_2_out, multiplexer_3_out, multiplexer_4_out, multiplexer_5_out,
       multiplexer_6_out, multiplexer_7_out, multiplexer_8_out, multiplexer_9_out, multiplexer_10_out,
       multiplexer_11_out, multiplexer_12_out, multiplexer_13_out, multiplexer_14_out, multiplexer_15_out,
       multiplexer_16_out;

  Multiplexer #(.enable("false")) multiplexer_1 (.in0(B1), .in1(V1), .out(multiplexer_1_out), .sel(Mode));
  Multiplexer #(.enable("false")) multiplexer_2 (.in0(B2), .in1(V2), .out(multiplexer_2_out), .sel(Mode));
  Multiplexer #(.enable("false")) multiplexer_3 (.in0(B3), .in1(V3), .out(multiplexer_3_out), .sel(Mode));
  Multiplexer #(.enable("false")) multiplexer_4 (.in0(B4), .in1(V4), .out(multiplexer_4_out), .sel(Mode));
  Multiplexer #(.enable("false")) multiplexer_5 (.in0(C1), .in1(W1), .out(multiplexer_5_out), .sel(Mode));
  Multiplexer #(.enable("false")) multiplexer_6 (.in0(C2), .in1(W2), .out(multiplexer_6_out), .sel(Mode));
  Multiplexer #(.enable("false")) multiplexer_7 (.in0(C3), .in1(W3), .out(multiplexer_7_out), .sel(Mode));
  Multiplexer #(.enable("false")) multiplexer_8 (.in0(C4), .in1(W4), .out(multiplexer_8_out), .sel(Mode));
  Multiplexer #(.enable("false")) multiplexer_9 (.in0(D1), .in1(X1), .out(multiplexer_9_out), .sel(Mode));
  Multiplexer #(.enable("false")) multiplexer_10 (.in0(D2), .in1(X2), .out(multiplexer_10_out), .sel(Mode));
  Multiplexer #(.enable("false")) multiplexer_11 (.in0(D3), .in1(X3), .out(multiplexer_11_out), .sel(Mode));
  Multiplexer #(.enable("false")) multiplexer_12 (.in0(D4), .in1(X4), .out(multiplexer_12_out), .sel(Mode));
  Multiplexer #(.enable("false")) multiplexer_13 (.in0(E1), .in1(Y1), .out(multiplexer_13_out), .sel(Mode));
  Multiplexer #(.enable("false")) multiplexer_14 (.in0(E2), .in1(Y2), .out(multiplexer_14_out), .sel(Mode));
  Multiplexer #(.enable("false")) multiplexer_15 (.in0(E3), .in1(Y3), .out(multiplexer_15_out), .sel(Mode));
  Multiplexer #(.enable("false")) multiplexer_16 (.in0(E4), .in1(Y4), .out(multiplexer_16_out), .sel(Mode));
  Shift_Register shift_register_1 (
    ._0(A1), ._1(A2), ._2(A3), ._3(A4), .Clk(Clk), .Clear(Clear), ._0_2(V1), ._1_2(V2), ._2_2(V3), ._3_2(V4));
  Shift_Register shift_register_2 (
    ._0(multiplexer_1_out), ._1(multiplexer_2_out), ._2(multiplexer_3_out), ._3(multiplexer_4_out),
    .Clk(Clk), .Clear(Clear), ._0_2(W1), ._1_2(W2), ._2_2(W3), ._3_2(W4));
  Shift_Register shift_register_3 (
    ._0(multiplexer_5_out), ._1(multiplexer_6_out), ._2(multiplexer_7_out), ._3(multiplexer_8_out),
    .Clk(Clk), .Clear(Clear), ._0_2(X1), ._1_2(X2), ._2_2(X3), ._3_2(X4));
  Shift_Register shift_register_4 (
    ._0(multiplexer_9_out), ._1(multiplexer_10_out), ._2(multiplexer_11_out), ._3(multiplexer_12_out),
    .Clk(Clk), .Clear(Clear), ._0_2(Y1), ._1_2(Y2), ._2_2(Y3), ._3_2(Y4));
  Shift_Register shift_register_5 (
    ._0(multiplexer_13_out), ._1(multiplexer_14_out), ._2(multiplexer_15_out), ._3(multiplexer_16_out),
    .Clk(Clk), .Clear(Clear), ._0_2(Z1), ._1_2(Z2), ._2_2(Z3), ._3_2(Z4));
endmodule

// Next'
module Next (
  input  X,
  input  Clk,
  input  Clear,
  output C,
  output B,
  output A
);

  wire and_1_out, and_2_out, and_3_out, and_4_out, and_5_out, and_6_out, and_7_out, d_ff_1_qn, d_ff_2_qn,
       d_ff_3_qn, not_1_out, not_2_out, or_1_out, or_2_out, or_3_out;

  not not_1 (not_1_out, X);
  not not_2 (not_2_out, B);
  and and_1 (and_1_out, A, not_2_out);
  and and_2 (and_2_out, X, C, B);
  and and_3 (and_3_out, B, not_1_out);
  and and_4 (and_4_out, B, d_ff_3_qn);
  and and_5 (and_5_out, X, C, d_ff_2_qn);
  or or_1 (or_1_out, and_1_out, and_2_out);
  and and_6 (and_6_out, C, not_1_out);
  and and_7 (and_7_out, X, d_ff_3_qn, d_ff_1_qn);
  or or_2 (or_2_out, and_3_out, and_4_out, and_5_out);
  or or_3 (or_3_out, and_6_out, and_7_out);
  D_Flip_Flop d_ff_1 (.clk(Clk), .D(or_1_out), .Q(A), .Qn(d_ff_1_qn), .reset(Clear));  // open: preset, en
  D_Flip_Flop d_ff_2 (.clk(Clk), .D(or_2_out), .Q(B), .Qn(d_ff_2_qn), .reset(Clear));  // open: preset, en
  D_Flip_Flop d_ff_3 (.clk(Clk), .D(or_3_out), .Q(C), .Qn(d_ff_3_qn), .reset(Clear));  // open: preset, en
endmodule

module password_select (
  input  in_1,
  input  in_2,
  input  in_3,
  output out_4,
  output out_5
);

  wire or_1_out;

  or or_1 (or_1_out, in_2, in_1, in_3);
  D_Flip_Flop d_ff_1 (.clk(or_1_out), .D(in_2), .Q(out_4));  // open: Qn, preset, en, reset
  D_Flip_Flop d_ff_2 (.clk(or_1_out), .D(in_3), .Q(out_5));  // open: Qn, preset, en, reset
endmodule

module Mr_Comparator (
  input  [3:0] A0,
  input  in_2,
  input  [3:0] B0,
  input  [3:0] A1,
  input  [3:0] B1,
  input  [3:0] A2,
  input  [3:0] B2,
  input  [3:0] A3,
  input  [3:0] B3,
  input  [3:0] A4,
  input  [3:0] B4,
  output A_B
);

  wire comparator_4_bit_1_a_b_3, comparator_4_bit_2_a_b_3, comparator_4_bit_3_a_b_3,
       comparator_4_bit_4_a_b_3, comparator_4_bit_5_a_b_3;

  comparator_4_bit comparator_4_bit_1 (.A(A0), .B(B0), .A_B_3(comparator_4_bit_1_a_b_3));  // open: A_B, A_B_2
  comparator_4_bit comparator_4_bit_2 (.A(A1), .B(B1), .A_B_3(comparator_4_bit_2_a_b_3));  // open: A_B, A_B_2
  comparator_4_bit comparator_4_bit_3 (.A(A2), .B(B2), .A_B_3(comparator_4_bit_3_a_b_3));  // open: A_B, A_B_2
  comparator_4_bit comparator_4_bit_4 (.A(A3), .B(B3), .A_B_3(comparator_4_bit_4_a_b_3));  // open: A_B, A_B_2
  comparator_4_bit comparator_4_bit_5 (.A(A4), .B(B4), .A_B_3(comparator_4_bit_5_a_b_3));  // open: A_B, A_B_2
  and and_1 (A_B, in_2, comparator_4_bit_1_a_b_3, comparator_4_bit_5_a_b_3, comparator_4_bit_2_a_b_3, comparator_4_bit_3_a_b_3, comparator_4_bit_4_a_b_3);
endmodule

module comparator_4_bit (
  input  [3:0] A,
  input  [3:0] B,
  output A_B,
  output A_B_2,
  output A_B_3
);

  wire and_1_out, and_2_out, and_3_out, and_4_out, and_5_out, and_6_out, and_7_out, and_8_out, and_9_out,
       and_10_out, and_11_out, and_12_out, and_13_out, and_15_out, not_1_out, not_2_out, not_3_out,
       not_4_out, not_5_out, not_6_out, not_7_out, not_8_out, xnor_1_out, xnor_2_out, xnor_3_out, xnor_4_out;

  and and_1 (and_1_out, not_1_out, B[3]);
  not not_1 (not_1_out, A[3]);
  not not_2 (not_2_out, B[3]);
  and and_2 (and_2_out, A[3], not_2_out);
  and and_3 (and_3_out, not_3_out, B[2]);
  not not_3 (not_3_out, A[2]);
  and and_4 (and_4_out, A[2], not_4_out);
  not not_4 (not_4_out, B[2]);
  not not_5 (not_5_out, A[1]);
  and and_5 (and_5_out, not_5_out, B[1]);
  and and_6 (and_6_out, A[1], not_6_out);
  not not_6 (not_6_out, B[1]);
  and and_7 (and_7_out, not_7_out, B[0]);
  not not_7 (not_7_out, A[0]);
  not not_8 (not_8_out, B[0]);
  and and_8 (and_8_out, A[0], not_8_out);
  xnor xnor_1 (xnor_1_out, and_1_out, and_2_out);
  xnor xnor_2 (xnor_2_out, and_3_out, and_4_out);
  xnor xnor_3 (xnor_3_out, and_5_out, and_6_out);
  xnor xnor_4 (xnor_4_out, and_7_out, and_8_out);
  and and_9 (and_9_out, xnor_1_out, and_3_out);
  and and_10 (and_10_out, xnor_1_out, and_4_out);
  and and_11 (and_11_out, xnor_1_out, xnor_2_out, and_5_out);
  and and_12 (and_12_out, xnor_1_out, xnor_2_out, and_6_out);
  and and_13 (and_13_out, xnor_1_out, xnor_2_out, xnor_3_out, and_7_out);
  and and_14 (A_B_3, xnor_1_out, xnor_2_out, xnor_3_out, xnor_4_out);
  and and_15 (and_15_out, xnor_1_out, xnor_2_out, xnor_3_out, and_8_out);
  or or_1 (A_B, and_1_out, and_9_out, and_11_out, and_13_out);
  or or_2 (A_B_2, and_2_out, and_10_out, and_12_out, and_15_out);

  // Notes on the sheet:
  //   X3
  //   X2
  //   X1
  //   X0
endmodule

module nots (
  input  in_1,
  output out_2
);

  wire not_1_out, not_2_out, not_3_out, not_4_out, not_5_out, not_6_out, not_7_out, not_8_out, not_9_out;

  not not_1 (not_1_out, in_1);
  not not_2 (not_2_out, not_3_out);
  not not_3 (not_3_out, not_1_out);
  not not_4 (not_4_out, not_2_out);
  not not_5 (not_5_out, not_6_out);
  not not_6 (not_6_out, not_4_out);
  not not_7 (not_7_out, not_5_out);
  not not_8 (not_8_out, not_7_out);
  not not_9 (not_9_out, not_8_out);
  not not_10 (out_2, not_9_out);
endmodule

module Timer (
  input  X,
  input  CLK,
  output out_3
);

  wire and_1_out, and_2_out, and_3_out, and_4_out, and_5_out, and_6_out, d_ff_1_q, d_ff_1_qn, d_ff_2_q,
       d_ff_2_qn, d_ff_3_q, d_ff_3_qn, not_1_out, or_1_out, or_2_out, or_3_out;

  not not_1 (not_1_out, X);
  and and_1 (and_1_out, d_ff_1_q, not_1_out);
  and and_2 (and_2_out, not_1_out, d_ff_3_q, d_ff_2_q);
  and and_3 (and_3_out, d_ff_1_qn, d_ff_2_qn, d_ff_3_q, not_1_out);
  and and_4 (and_4_out, d_ff_2_q, d_ff_3_qn, not_1_out);
  and and_5 (and_5_out, d_ff_1_q, not_1_out);
  and and_6 (and_6_out, not_1_out, d_ff_3_qn);
  or or_1 (or_1_out, and_1_out, and_2_out);
  or or_2 (or_2_out, and_3_out, and_4_out);
  or or_3 (or_3_out, and_5_out, and_6_out);
  D_Flip_Flop d_ff_1 (.clk(CLK), .D(or_1_out), .Q(d_ff_1_q), .Qn(d_ff_1_qn));  // open: preset, en, reset
  D_Flip_Flop d_ff_2 (.clk(CLK), .D(or_2_out), .Q(d_ff_2_q), .Qn(d_ff_2_qn));  // open: preset, en, reset
  D_Flip_Flop d_ff_3 (.clk(CLK), .D(or_3_out), .Q(d_ff_3_q), .Qn(d_ff_3_qn));  // open: preset, en, reset
  or or_4 (out_3, d_ff_1_qn, d_ff_3_qn, X);
endmodule
